// Logisim project Johnson.circ as structural Verilog: 2 circuits, main circuit main
module main (
);

  wire button_1_out, button_2_out, clkjk_1_nq, clkjk_1_q, clkjk_2_nq, clkjk_2_q, clkjk_3_nq, clkjk_3_q,
       clkjk_4_nq, clkjk_4_q, clkjk_5_nq, clkjk_5_q, clkjk_6_nq, clkjk_6_q, nor_1_out, nor_2_out, nor_3_out,
       nor_4_out, nor_5_out, nor_6_out, nor_7_out, nor_8_out, nor_9_out, nor_10_out, nor_11_out, nor_12_out;

  Button button_1 (.out(button_1_out));
  Button button_2 (.out(button_2_out));
  CLKJK clkjk_1 (.CLK(button_1_out), .J(clkjk_6_nq), .K(clkjk_6_q), ._0(button_2_out), .Q(clkjk_1_q), .nQ(clkjk_1_nq));
  LED led_1 (.in(clkjk_1_q));
  CLKJK clkjk_2 (.CLK(button_1_out), .J(clkjk_1_q), .K(clkjk_1_nq), ._0(button_2_out), .Q(clkjk_2_q), .nQ(clkjk_2_nq));
  LED led_2 (.in(clkjk_2_q));
  LED led_3 (.in(clkjk_3_q));
  CLKJK clkjk_3 (.CLK(button_1_out), .J(clkjk_2_q), .K(clkjk_2_nq), ._0(button_2_out), .Q(clkjk_3_q), .nQ(clkjk_3_nq));
  LED led_4 (.in(clkjk_4_q));
  CLKJK clkjk_4 (.CLK(button_1_out), .J(clkjk_3_q), .K(clkjk_3_nq), ._0(button_2_out), .Q(clkjk_4_q), .nQ(clkjk_4_nq));
  LED led_5 (.in(clkjk_5_q));
  CLKJK clkjk_5 (.CLK(button_1_out), .J(clkjk_4_q), .K(clkjk_4_nq), ._0(button_2_out), .Q(clkjk_5_q), .nQ(clkjk_5_nq));
  LED led_6 (.in(clkjk_6_q));
  CLKJK clkjk_6 (.CLK(button_1_out), .J(clkjk_5_q), .K(clkjk_5_nq), ._0(button_2_out), .Q(clkjk_6_q), .nQ(clkjk_6_nq));
  nor nor_1 (nor_1_out, clkjk_1_q, clkjk_6_q);
  nor nor_2 (nor_2_out, clkjk_1_nq, clkjk_2_q);
  nor nor_3 (nor_3_out, clkjk_2_nq, clkjk_3_q);
  nor nor_4 (nor_4_out, clkjk_3_nq, clkjk_4_q);
  nor nor_5 (nor_5_out, clkjk_4_nq, clkjk_5_q);
  nor nor_6 (nor_6_out, clkjk_5_nq, clkjk_6_q);
  nor nor_7 (nor_7_out, clkjk_1_nq, clkjk_6_nq);
  nor nor_8 (nor_8_out, clkjk_1_q, clkjk_2_nq);
  nor nor_9 (nor_9_out, clkjk_2_q, clkjk_3_nq);
  nor nor_10 (nor_10_out, clkjk_3_q, clkjk_4_nq);
  nor nor_11 (nor_11_out, clkjk_4_q, clkjk_5_nq);
  nor nor_12 (nor_12_out, clkjk_5_q, clkjk_6_nq);
  LED led_7 (.in(nor_1_out));
  LED led_8 (.in(nor_2_out));
  LED led_9 (.in(nor_3_out));
  LED led_10 (.in(nor_4_out));
  LED led_11 (.in(nor_5_out));
  LED led_12 (.in(nor_6_out));
  LED led_13 (.in(nor_7_out));
  LED led_14 (.in(nor_8_out));
  LED led_15 (.in(nor_9_out));
  LED led_16 (.in(nor_10_out));
  LED led_17 (.in(nor_11_out));
  LED led_18 (.in(nor_12_out));

  // Notes on the sheet:
  //   0
  //   1
  //   2
  //   3
  //   4
  //   5
  //   6
  //   7
  //   8
  //   9
  //   10
  //   11
endmodule

module CLKJK (
  input  CLK,
  input  J,
  input  K,
  input  _0,
  output Q,
  output nQ
);

  wire nor_1_out, nor_2_out, nor_3_out, nor_4_out, nor_5_out, nor_6_out, not_1_out;

  not not_1 (not_1_out, CLK);
  nor nor_1 (nor_1_out, J, CLK);
  nor nor_2 (nor_2_out, CLK, K);
  nor nor_3 (nor_3_out, nor_1_out, _0, nor_4_out);
  nor nor_4 (nor_4_out, nor_3_out, nor_2_out);
  nor nor_5 (nor_5_out, nor_3_out, not_1_out);
  nor nor_6 (nor_6_out, not_1_out, nor_4_out);
  nor nor_7 (Q, nor_5_out, _0, nQ);
  nor nor_8 (nQ, Q, nor_6_out);
endmodule
