// Logisim project ShiftRegister.circ as structural Verilog: 6 circuits, main circuit main
module main (
  input  Op2,
  input  Op1,
  input  SerialIn
);

  wire Clock_out, dir_1_d, dir_2_d, dir_3_d, dir_4_d, dir_5_d, dir_6_d, dir_7_d, dir_8_d, reg_1_q, reg_2_q,
       reg_3_q, reg_4_q, reg_5_q, reg_6_q, reg_7_q, reg_8_q;

  Dir dir_1 (.P(SerialIn), .D(dir_1_d), .N(reg_1_q), .Op1(Op2), .Op2(Op1), .V(1'b0));  // open: W
  Button Clock (.out(Clock_out));
  Dir dir_2 (.P(reg_1_q), .D(dir_2_d), .N(reg_4_q), .Op1(Op2), .Op2(Op1), .V(1'b1));  // open: W
  Dir dir_3 (.P(reg_2_q), .D(dir_3_d), .N(reg_3_q), .Op1(Op2), .Op2(Op1), .V(1'b0));  // open: W
  Reg reg_1 (.D(dir_3_d), .CLK(Clock_out), .Q(reg_1_q));  // open: nQ
  Reg reg_2 (.D(dir_1_d), .CLK(Clock_out), .Q(reg_2_q));  // open: nQ
  LED led_1 (.in(reg_2_q));
  Dir dir_4 (.P(reg_3_q), .D(dir_4_d), .N(reg_5_q), .Op1(Op2), .Op2(Op1), .V(1'b1));  // open: W
  Reg reg_3 (.D(dir_2_d), .CLK(Clock_out), .Q(reg_3_q));  // open: nQ
  LED led_2 (.in(reg_1_q));
  LED led_3 (.in(reg_3_q));
  Dir dir_5 (.P(reg_4_q), .D(dir_5_d), .N(reg_6_q), .Op1(Op2), .Op2(Op1), .V(1'b1));  // open: W
  Reg reg_4 (.D(dir_4_d), .CLK(Clock_out), .Q(reg_4_q));  // open: nQ
  LED led_4 (.in(reg_4_q));
  Dir dir_6 (.P(reg_5_q), .D(dir_6_d), .N(reg_7_q), .Op1(Op2), .Op2(Op1), .V(1'b0));  // open: W
  Reg reg_5 (.D(dir_5_d), .CLK(Clock_out), .Q(reg_5_q));  // open: nQ
  LED led_5 (.in(reg_5_q));
  Dir dir_7 (.P(reg_6_q), .D(dir_7_d), .N(reg_8_q), .Op1(Op2), .Op2(Op1), .V(1'b0));  // open: W
  Reg reg_6 (.D(dir_6_d), .CLK(Clock_out), .Q(reg_6_q));  // open: nQ
  LED led_6 (.in(reg_6_q));
  Dir dir_8 (.P(reg_7_q), .D(dir_8_d), .N(1'b0), .Op1(Op2), .Op2(Op1), .V(1'b0));  // open: W
  Reg reg_7 (.D(dir_7_d), .CLK(Clock_out), .Q(reg_7_q));  // open: nQ
  LED led_7 (.in(reg_7_q));
  Reg reg_8 (.D(dir_8_d), .CLK(Clock_out), .Q(reg_8_q));  // open: nQ
  LED led_8 (.in(reg_8_q));

  // Notes on the sheet:
  //   00=Right  01=N  10=Load
endmodule

module Reg (
  input  D,
  input  CLK,
  output Q,
  output nQ
);

  wire _1_out, _2_out, _3_out, _4_out, _5_out, _6_out, not_1_out, not_2_out;

  not not_1 (not_1_out, D);
  not not_2 (not_2_out, CLK);
  nor _1 (_1_out, D, not_2_out);
  nor _2 (_2_out, not_1_out, not_2_out);
  nor _3 (_3_out, _1_out, _4_out);
  nor _4 (_4_out, _3_out, _2_out);
  nor _5 (_5_out, CLK, _3_out);
  nor _7 (Q, _5_out, nQ);
  nor _8 (nQ, Q, _6_out);
  nor _6 (_6_out, _4_out, CLK);
endmodule

module Dir (
  input  Op1,
  input  Op2,
  input  P,
  input  N,
  input  V,
  input  W,
  output D
);

  wire nor_1_out, nor_2_out, nor_3_out, nor_4_out, not_1_out, not_2_out;

  not not_1 (not_1_out, Op1);
  not not_2 (not_2_out, Op2);
  nor nor_1 (nor_1_out, P, Op1, Op2);
  nor nor_2 (nor_2_out, N, Op1, not_2_out);
  nor nor_3 (nor_3_out, V, not_1_out, Op2);
  nor nor_4 (nor_4_out, W, not_1_out, not_2_out);
  nor nor_5 (D, nor_1_out, nor_2_out, nor_3_out, nor_4_out);

  // Notes on the sheet:
  //   00=P  01=N  10=V
endmodule

module PCB (
  input  CLK,
  input  Op2,
  input  Op1,
  input  Prev0,
  input  Next0,
  input  Load0A,
  input  Load0B,
  input  Prev1,
  input  Next1,
  input  Load1A,
  input  Load1B,
  input  Prev2,
  input  Next2,
  input  Load2A,
  input  Load2B,
  input  Prev3,
  input  Next3,
  input  Load3A,
  input  Load3B,
  output Q0,
  output nQ0,
  output Q1,
  output nQ1,
  output Q2,
  output nQ2,
  output Q3,
  output nQ3
);

  wire _1_2_out, _1_3_out, _1_4_out, _1_out, _2_2_out, _2_3_out, _2_4_out, _2_out, _3_2_out, _3_3_out,
       _3_4_out, _3_out, _4_2_out, _4_3_out, _4_4_out, _4_out, _5_2_out, _5_3_out, _5_4_out, _5_out,
       _6_2_out, _6_3_out, _6_4_out, _6_out, nor_1_out, nor_2_out, nor_3_out, nor_4_out, nor_5_out,
       nor_6_out, nor_7_out, nor_8_out, nor_9_out, nor_10_out, nor_11_out, nor_12_out, nor_13_out,
       nor_14_out, nor_15_out, nor_16_out, nor_17_out, nor_18_out, nor_19_out, nor_20_out, not_1_out,
       not_2_out, not_3_out, not_4_out, not_5_out, not_6_out, not_7_out;

  not not_1 (not_1_out, CLK);
  not not_2 (not_2_out, Op2);
  not not_3 (not_3_out, Op1);
  nor nor_1 (nor_1_out, Prev0, Op1, Op2);
  nor nor_2 (nor_2_out, Next0, Op1, not_2_out);
  nor nor_3 (nor_3_out, Load0A, not_3_out, Op2);
  nor nor_4 (nor_4_out, Load0B, not_3_out, not_2_out);
  nor nor_5 (nor_5_out, Prev1, Op1, Op2);
  nor nor_6 (nor_6_out, Next1, Op1, not_2_out);
  nor nor_7 (nor_7_out, Load1A, not_3_out, Op2);
  nor nor_8 (nor_8_out, Load1B, not_3_out, not_2_out);
  nor nor_9 (nor_9_out, Prev2, Op1, Op2);
  nor nor_10 (nor_10_out, Next2, Op1, not_2_out);
  nor nor_11 (nor_11_out, Load2A, not_3_out, Op2);
  nor nor_12 (nor_12_out, Load2B, not_3_out, not_2_out);
  nor nor_13 (nor_13_out, Prev3, Op1, Op2);
  nor nor_14 (nor_14_out, Next3, Op1, not_2_out);
  nor nor_15 (nor_15_out, Load3A, not_3_out, Op2);
  nor nor_16 (nor_16_out, Load3B, not_3_out, not_2_out);
  nor nor_17 (nor_17_out, nor_1_out, nor_2_out, nor_3_out, nor_4_out);
  nor nor_18 (nor_18_out, nor_5_out, nor_6_out, nor_7_out, nor_8_out);
  nor nor_19 (nor_19_out, nor_9_out, nor_10_out, nor_11_out, nor_12_out);
  nor nor_20 (nor_20_out, nor_13_out, nor_14_out, nor_15_out, nor_16_out);
  not not_4 (not_4_out, nor_17_out);
  not not_5 (not_5_out, nor_18_out);
  not not_6 (not_6_out, nor_19_out);
  not not_7 (not_7_out, nor_20_out);
  nor _1 (_1_out, nor_17_out, not_1_out);
  nor _3 (_3_out, _1_out, _4_out);
  nor _4 (_4_out, _3_out, _2_out);
  nor _2 (_2_out, not_4_out, not_1_out);
  nor _1_2 (_1_2_out, nor_18_out, not_1_out);
  nor _3_2 (_3_2_out, _1_2_out, _4_2_out);
  nor _4_2 (_4_2_out, _3_2_out, _2_2_out);
  nor _2_2 (_2_2_out, not_5_out, not_1_out);
  nor _1_3 (_1_3_out, nor_19_out, not_1_out);
  nor _3_3 (_3_3_out, _1_3_out, _4_3_out);
  nor _4_3 (_4_3_out, _3_3_out, _2_3_out);
  nor _2_3 (_2_3_out, not_6_out, not_1_out);
  nor _1_4 (_1_4_out, nor_20_out, not_1_out);
  nor _3_4 (_3_4_out, _1_4_out, _4_4_out);
  nor _4_4 (_4_4_out, _3_4_out, _2_4_out);
  nor _2_4 (_2_4_out, not_7_out, not_1_out);
  nor _5 (_5_out, CLK, _3_out);
  nor _6 (_6_out, _4_out, CLK);
  nor _5_2 (_5_2_out, CLK, _3_2_out);
  nor _6_2 (_6_2_out, _4_2_out, CLK);
  nor _5_3 (_5_3_out, CLK, _3_3_out);
  nor _6_3 (_6_3_out, _4_3_out, CLK);
  nor _5_4 (_5_4_out, CLK, _3_4_out);
  nor _6_4 (_6_4_out, _4_4_out, CLK);
  nor _7 (Q0, _5_out, nQ0);
  nor _8 (nQ0, Q0, _6_out);
  nor _7_2 (Q1, _5_2_out, nQ1);
  nor _8_2 (nQ1, Q1, _6_2_out);
  nor _7_3 (Q2, _5_3_out, nQ2);
  nor _8_3 (nQ2, Q2, _6_3_out);
  nor _7_4 (Q3, _5_4_out, nQ3);
  nor _8_4 (nQ3, Q3, _6_4_out);

  // Notes on the sheet:
  //   3
  //   36
  //   16
  //   4
  //   16
  //   16
  //   16
  //   135 Transistors 58 Resistors
  //   7 pcs INV
  //   32 pcs NOR2
  //   16 pcs NOR3
  //   4 pcs NOR4
  //   16
endmodule

module PCBbus (
  input  CLK,
  input  Op2,
  input  Op1,
  input  [3:0] LoadB,
  input  [3:0] LoadA,
  input  [3:0] Next,
  input  [3:0] Prev,
  output [3:0] Q,
  output [3:0] Q_2
);

  PCB pcb_1 (
    .CLK(CLK), .Op2(Op2), .Op1(Op1), .Prev0(Prev[0]), .Next0(Next[0]), .Load0A(LoadA[0]), .Load0B(LoadB[0]),
    .Prev1(Prev[1]), .Next1(Next[1]), .Load1A(LoadA[1]), .Load1B(LoadB[1]), .Prev2(Prev[2]), .Next2(Next[2]),
    .Load2A(LoadA[2]), .Load2B(LoadB[2]), .Prev3(Prev[3]), .Next3(Next[3]), .Load3A(LoadA[3]),
    .Load3B(LoadB[3]), .Q0(Q[0]), .nQ0(Q_2[0]), .Q1(Q[1]), .nQ1(Q_2[1]), .Q2(Q[2]), .nQ2(Q_2[2]), .Q3(Q[3]),
    .nQ3(Q_2[3]));
endmodule

module PCBbusMain (
  input  [1:0] in_1,
  input  [3:0] Serial
);

  wire CLK_out;
  wire [3:0] pcbbus_1_q, pcbbus_2_q, pcbbus_3_q, pcbbus_4_q, pcbbus_5_q, pcbbus_6_q, pcbbus_7_q, pcbbus_8_q,
       undriven;

  Button CLK (.out(CLK_out));
  PCBbus pcbbus_1 (
    .CLK(CLK_out), .Op2(in_1[1]), .Op1(in_1[0]), .LoadB(4'b0000), .LoadA(undriven), .Next(pcbbus_2_q),
    .Prev(Serial), .Q(pcbbus_1_q));  // open: Q_2
  // Probe on pcbbus_1_q
  PCBbus pcbbus_2 (
    .CLK(CLK_out), .Op2(in_1[1]), .Op1(in_1[0]), .LoadB(4'b0000), .Next(pcbbus_3_q), .Prev(pcbbus_1_q),
    .Q(pcbbus_2_q));  // open: LoadA, Q_2
  // Probe on pcbbus_2_q
  PCBbus pcbbus_3 (
    .CLK(CLK_out), .Op2(in_1[1]), .Op1(in_1[0]), .LoadB(4'b0000), .Next(pcbbus_4_q), .Prev(pcbbus_2_q),
    .Q(pcbbus_3_q));  // open: LoadA, Q_2
  // Probe on pcbbus_3_q
  PCBbus pcbbus_4 (
    .CLK(CLK_out), .Op2(in_1[1]), .Op1(in_1[0]), .LoadB(4'b0000), .Next(pcbbus_5_q), .Prev(pcbbus_3_q),
    .Q(pcbbus_4_q));  // open: LoadA, Q_2
  // Probe on pcbbus_4_q
  PCBbus pcbbus_5 (
    .CLK(CLK_out), .Op2(in_1[1]), .Op1(in_1[0]), .LoadB(4'b0000), .Next(pcbbus_6_q), .Prev(pcbbus_4_q),
    .Q(pcbbus_5_q));  // open: LoadA, Q_2
  // Probe on pcbbus_5_q
  PCBbus pcbbus_6 (
    .CLK(CLK_out), .Op2(in_1[1]), .Op1(in_1[0]), .LoadB(4'b0000), .Next(pcbbus_7_q), .Prev(pcbbus_5_q),
    .Q(pcbbus_6_q));  // open: LoadA, Q_2
  // Probe on pcbbus_6_q
  PCBbus pcbbus_7 (
    .CLK(CLK_out), .Op2(in_1[1]), .Op1(in_1[0]), .LoadB(4'b0000), .Next(pcbbus_8_q), .Prev(pcbbus_6_q),
    .Q(pcbbus_7_q));  // open: LoadA, Q_2
  // Probe on pcbbus_7_q
  PCBbus pcbbus_8 (
    .CLK(CLK_out), .Op2(in_1[1]), .Op1(in_1[0]), .LoadB(4'b0000), .Next(4'b1111), .Prev(pcbbus_7_q),
    .Q(pcbbus_8_q));  // open: LoadA, Q_2
  // Probe on pcbbus_8_q

  // Notes on the sheet:
  //   00=Right   10=Left   01=LoadA   11=LoadB
endmodule
